// Logisim project AXLE_COUNTER.circ as structural Verilog: 1 circuit, main circuit main
module main (
  input  WHEEL_IN_COUNTER,
  input  WHEEL_OUT_COUNTER,
  input  WHEEL_IN_HEALTH_COUNTER,
  input  WHEEL_OUT_HEALTH_COUNTER,
  input  SECTION_COUNTER_CLEAR,
  input  ENGINEER_OFFSHOT_RESET
);

  wire and_1_out, and_2_out, and_3_out, comparator_1_eq, comparator_1_gt, comparator_1_lt, counter_1_carry,
       counter_2_carry, not_1_out, not_2_out, not_3_out, not_4_out, not_5_out, not_6_out, not_7_out,
       or_1_out, or_2_out, or_3_out, or_4_out, or_5_out;
  wire [2:0] counter_1_q, counter_2_q;

  Counter #(.max('h7), .width(3)) counter_1 (
    .clr(and_1_out), .clk(WHEEL_IN_COUNTER), .carry(counter_1_carry), .Q(counter_1_q));  // open: load, up, count, D
  or or_1 (or_1_out, SECTION_COUNTER_CLEAR, ENGINEER_OFFSHOT_RESET);
  LED WHEEL_IN_LIMIT_OFF_SHOOT (.in(counter_1_carry));
  LED WHEEL_OUT_LIMIT_OFF_SHOOT (.in(counter_2_carry));
  not not_1 (not_1_out, or_1_out);
  not not_2 (not_2_out, WHEEL_IN_HEALTH_COUNTER);
  not not_3 (not_3_out, WHEEL_OUT_HEALTH_COUNTER);
  LED WHEEL_OUT_COUNTER_STATUS_LED (.in(not_3_out));
  LED WHEEL_IN_COUNTER_STATUS_LED (.in(not_2_out));
  and and_1 (and_1_out, not_4_out, not_5_out, not_6_out);
  not not_4 (not_4_out, and_2_out);
  not not_5 (not_5_out, or_5_out);
  not not_6 (not_6_out, and_3_out);
  and and_2 (and_2_out, not_1_out, WHEEL_IN_HEALTH_COUNTER, WHEEL_OUT_HEALTH_COUNTER);
  Comparator #(.mode("unsigned"), .width(3)) comparator_1 (
    .a(counter_1_q), .b(counter_2_q), .gt(comparator_1_gt), .eq(comparator_1_eq), .lt(comparator_1_lt));
  Counter #(.max('h7), .width(3)) counter_2 (
    .clr(and_1_out), .clk(WHEEL_OUT_COUNTER), .carry(counter_2_carry), .Q(counter_2_q));  // open: load, up, count, D
  or or_2 (or_2_out, counter_1_carry, counter_2_carry);
  not not_7 (not_7_out, comparator_1_eq);
  or or_3 (or_3_out, comparator_1_gt, comparator_1_lt);
  and and_3 (and_3_out, or_3_out, not_7_out);
  or or_4 (or_4_out, not_3_out, not_2_out);
  LED COUNTER_RESET_STATUS (.in(or_1_out));
  or or_5 (or_5_out, and_3_out, or_2_out, or_4_out);
  LED SECTION_BLOCK_OCCUPANCY_STATUS (.in(or_5_out));

  // Notes on the sheet:
  //   SENSOR INPUTS
  //   MAINTANANCE OUTPUTS
  //   THIS AXLE COUNTER CAN COUNT AND COMPARE WHEEL SETS IN BOTH BIRECTIONS.
  //   NOTE: STATUS LEDS WILL SHOW GREEN IF SENSOR IS HEALTHY ELSE RED. IT IS A MAINTAINANCE WARNER.
  //   NOTE: WHEEL IN AND OUT COUNTER COUNTS THE NUMBER OF WHEELS ENTERING AND LEAVING A PARTICULAR SECTION.
  //   IF THE VALUE OF TWO COUNTER IS SAME THEN ONLY THE SECTION BLOCK WILL BE FREE ELSE RED LED WILL BE ON STATING THE SECTION IS OCCUPIED. 
  //   For better use use this design in real life 3 times per axle counter unit with different power and firewall with total distinct senors . And only clear if this satisfies 2oo3 category.
  //   OPERATIONAL OUTPUTS
endmodule
