// Logisim project Automatic_block_section_design.circ as structural Verilog: 1 circuit, main circuit main
module main (
  input  BLOCK_A_BIT_1,
  input  BLOCK_A_BIT_2,
  input  BLOCK_B_BIT_1,
  input  BLOCK_B_BIT_2,
  input  BLOCK_C_BIT_1,
  input  BLOCK_C_BIT_2,
  input  BLOCK_D_BIT_1,
  input  BLOCK_D_BIT_2
);

  wire and_1_out, and_2_out, and_3_out, and_4_out, and_5_out, and_6_out, and_7_out, and_8_out, and_9_out,
       not_1_out, not_2_out, not_3_out, not_4_out, not_5_out, not_6_out, not_7_out, not_8_out, not_9_out,
       not_10_out, or_1_out, or_2_out, or_3_out;

  not not_1 (not_1_out, BLOCK_A_BIT_2);
  not not_2 (not_2_out, BLOCK_B_BIT_2);
  not not_3 (not_3_out, BLOCK_C_BIT_2);
  and and_1 (and_1_out, BLOCK_A_BIT_1, not_1_out);
  not not_4 (not_4_out, and_1_out);
  and and_2 (and_2_out, BLOCK_B_BIT_1, not_2_out);
  and and_3 (and_3_out, BLOCK_C_BIT_1, not_3_out);
  not not_5 (not_5_out, BLOCK_D_BIT_2);
  and and_4 (and_4_out, not_4_out, and_2_out);
  not not_6 (not_6_out, and_4_out);
  and and_5 (and_5_out, BLOCK_D_BIT_1, not_5_out);
  not not_7 (not_7_out, and_1_out);
  not not_8 (not_8_out, and_1_out);
  and and_6 (and_6_out, not_6_out, and_3_out);
  not not_9 (not_9_out, and_6_out);
  and and_7 (and_7_out, not_7_out, and_4_out);
  and and_8 (and_8_out, not_8_out, and_6_out);
  and and_9 (and_9_out, not_9_out, and_5_out);
  or or_1 (or_1_out, and_7_out, and_8_out);
  LED BLOCK_A_DANGER (.in(or_2_out));
  or or_2 (or_2_out, and_1_out, not_10_out);
  LED BLOCK_A_CAUTION_OR_ATTENTION (.in(or_1_out));
  LED BLOCK_A_PROCEED (.in(and_9_out));
  LED BLOCK_A_ATTENTION (.in(and_8_out));
  or or_3 (or_3_out, and_9_out, or_1_out, and_8_out);
  not not_10 (not_10_out, or_3_out);

  // Notes on the sheet:
  //   NOTE: HERE ALL BIT 1'S ARE WHEEL IN COUNTERS AND 2'S ARE ALL OUT COUNTERS IN UP DIRECTION AND VICE  VERSA IN DOWN DIRECTION RESPECTIVELY. HERE IT IS SHOWN FOR ONE WAY ONLY.
endmodule
