// Logisim project Basic_Station_Section_Interlocking_Design.circ as structural Verilog: 1 circuit, main circuit main
module main (
  input  SC_HSF_SETTING_STATUS,
  input  SC_HSF_SETTING_OCCUPIED_STATUS,
  input  ML_HSF_SETTING_STATUS,
  input  ML_HSF_OCCUPIED_STATUS,
  input  LL_HSF_SETTING_STATUS,
  input  LL_HSF_OCCUPIED_STATUS,
  input  SC_SSF_SETTING_STATUS,
  input  SC_SSF_SETTING_OCCUPIED_STATUS,
  input  ML_SSF_SETTING_STATUS,
  input  ML_SSF_OCCUPIED_STATUS,
  input  ML_Ad_S_SETTING_STATUS,
  input  ML_Ad_SETTING_OCCUPIED_STATUS,
  input  OCCUPIED_STATUS,
  input  SC_LL_SSF_SETTING_STATUS,
  input  SC_LL_SSF_OCCUPANCY_STATUS,
  input  BLOCK_A_1_BIT,
  input  BLOCK_A_2_BIT
);

  wire and_1_out, and_2_out, and_3_out, and_4_out, and_5_out, and_6_out, and_7_out, and_8_out, and_9_out,
       and_10_out, and_11_out, and_12_out, and_13_out, and_14_out, and_15_out, and_16_out, and_17_out,
       and_18_out, and_19_out, and_20_out, and_21_out, and_22_out, and_23_out, and_24_out, and_25_out,
       and_26_out, and_27_out, and_28_out, and_29_out, and_30_out, and_31_out, not_1_out, not_2_out,
       not_3_out, not_4_out, not_5_out, not_6_out, not_7_out, not_8_out, not_9_out, not_10_out, not_11_out,
       not_12_out, not_13_out, not_14_out, not_15_out, not_16_out, not_17_out, not_18_out, not_19_out,
       not_20_out, not_21_out, not_22_out, not_23_out, not_24_out, not_25_out, not_26_out, not_27_out,
       not_28_out, not_29_out, not_30_out, not_31_out, not_32_out, not_33_out, or_1_out, or_2_out, or_3_out,
       or_4_out, or_5_out, or_6_out, or_7_out;

  not not_1 (not_1_out, SC_HSF_SETTING_OCCUPIED_STATUS);
  not not_2 (not_2_out, ML_HSF_OCCUPIED_STATUS);
  not not_3 (not_3_out, LL_HSF_OCCUPIED_STATUS);
  not not_4 (not_4_out, SC_SSF_SETTING_OCCUPIED_STATUS);
  not not_5 (not_5_out, OCCUPIED_STATUS);
  not not_6 (not_6_out, SC_HSF_SETTING_STATUS);
  not not_7 (not_7_out, not_1_out);
  not not_8 (not_8_out, SC_SSF_SETTING_STATUS);
  not not_9 (not_9_out, not_4_out);
  not not_10 (not_10_out, not_4_out);
  not not_11 (not_11_out, not_12_out);
  not not_12 (not_12_out, ML_SSF_OCCUPIED_STATUS);
  not not_13 (not_13_out, not_14_out);
  not not_14 (not_14_out, ML_Ad_SETTING_OCCUPIED_STATUS);
  not not_15 (not_15_out, SC_LL_SSF_SETTING_STATUS);
  and and_1 (and_1_out, not_15_out, SC_LL_SSF_OCCUPANCY_STATUS);
  not not_16 (not_16_out, not_4_out);
  not not_17 (not_17_out, BLOCK_A_2_BIT);
  and and_2 (and_2_out, not_6_out, not_7_out);
  and and_3 (and_3_out, LL_HSF_SETTING_STATUS, not_18_out);
  not not_18 (not_18_out, not_3_out);
  and and_4 (and_4_out, not_8_out, not_9_out);
  and and_5 (and_5_out, SC_SSF_SETTING_STATUS, not_10_out);
  and and_6 (and_6_out, ML_SSF_SETTING_STATUS, not_11_out);
  and and_7 (and_7_out, ML_Ad_S_SETTING_STATUS, not_13_out);
  and and_8 (and_8_out, BLOCK_A_1_BIT, BLOCK_A_2_BIT);
  or or_1 (or_1_out, and_8_out, and_9_out);
  and and_9 (and_9_out, BLOCK_A_1_BIT, not_17_out);
  not not_19 (not_19_out, or_1_out);
  not not_20 (not_20_out, and_1_out);
  and and_10 (and_10_out, and_1_out, and_11_out);
  and and_11 (and_11_out, not_16_out, SC_SSF_SETTING_STATUS);
  and and_12 (and_12_out, SC_HSF_SETTING_STATUS, not_7_out);
  LED led_1 (.in(and_12_out));
  LED led_2 (.in(and_12_out));
  LED led_3 (.in(not_5_out));
  LED led_4 (.in(not_5_out));
  LED led_5 (.in(not_5_out));
  LED led_6 (.in(not_21_out));
  LED led_7 (.in(not_1_out));
  not not_21 (not_21_out, not_1_out);
  not not_22 (not_22_out, and_13_out);
  and and_13 (and_13_out, and_4_out, and_6_out);
  not not_23 (not_23_out, or_6_out);
  and and_14 (and_14_out, and_10_out, and_6_out);
  not not_24 (not_24_out, and_14_out);
  not not_25 (not_25_out, and_15_out);
  and and_15 (and_15_out, and_7_out, or_1_out);
  not not_26 (not_26_out, not_2_out);
  and and_16 (and_16_out, and_12_out, and_3_out);
  LED led_8 (.in(not_3_out));
  LED led_9 (.in(not_3_out));
  LED led_10 (.in(not_3_out));
  LED led_11 (.in(and_3_out));
  LED led_12 (.in(and_3_out));
  LED led_13 (.in(and_3_out));
  LED led_14 (.in(and_2_out));
  LED led_15 (.in(and_2_out));
  LED led_16 (.in(and_21_out));
  LED led_17 (.in(and_21_out));
  LED led_18 (.in(not_2_out));
  LED led_19 (.in(not_2_out));
  LED led_20 (.in(not_2_out));
  not not_27 (not_27_out, and_17_out);
  and and_17 (and_17_out, and_13_out, and_7_out);
  and and_18 (and_18_out, and_17_out, or_1_out);
  or or_2 (or_2_out, or_6_out, not_19_out, not_24_out);
  and and_19 (and_19_out, not_23_out, and_14_out);
  and and_20 (and_20_out, and_19_out, or_1_out);
  or or_3 (or_3_out, not_19_out, not_25_out);
  not not_28 (not_28_out, or_3_out);
  and and_21 (and_21_out, ML_HSF_SETTING_STATUS, not_26_out);
  or or_4 (or_4_out, and_5_out, not_20_out);
  LED led_21 (.in(not_3_out));
  LED led_22 (.in(not_3_out));
  LED led_23 (.in(and_3_out));
  LED led_24 (.in(and_3_out));
  LED led_25 (.in(and_3_out));
  LED led_26 (.in(or_4_out));
  LED led_27 (.in(and_21_out));
  LED led_28 (.in(and_21_out));
  LED led_29 (.in(and_4_out));
  LED led_30 (.in(and_4_out));
  LED led_31 (.in(not_2_out));
  LED led_32 (.in(not_2_out));
  LED led_33 (.in(not_2_out));
  not not_29 (not_29_out, not_22_out);
  and and_22 (and_22_out, and_13_out, not_27_out);
  or or_5 (or_5_out, and_22_out, not_19_out);
  or or_6 (or_6_out, and_18_out, and_26_out);
  not not_30 (not_30_out, or_2_out);
  and and_23 (and_23_out, not_30_out, and_20_out);
  and and_24 (and_24_out, not_28_out, and_15_out);
  and and_25 (and_25_out, and_2_out, and_21_out);
  LED led_34 (.in(not_20_out));
  LED led_35 (.in(not_20_out));
  LED led_36 (.in(not_20_out));
  LED led_37 (.in(and_5_out));
  LED led_38 (.in(not_5_out));
  LED led_39 (.in(and_6_out));
  LED led_40 (.in(not_31_out));
  LED led_41 (.in(not_5_out));
  LED led_42 (.in(not_12_out));
  LED led_43 (.in(not_4_out));
  not not_31 (not_31_out, not_4_out);
  LED ML_SS_DANGER (.in(not_22_out));
  and and_26 (and_26_out, not_29_out, or_5_out);
  LED ML_SS_CAUTION (.in(and_26_out));
  LED ML_SS_PROCEED (.in(and_18_out));
  LED LL_SS_DANGER (.in(or_2_out));
  LED LL_SS_CAUTION (.in(and_23_out));
  LED Ad_SS_DANGER (.in(or_3_out));
  LED Ad_SS_PROCEED (.in(and_24_out));
  not not_32 (not_32_out, or_7_out);
  or or_7 (or_7_out, and_25_out, and_16_out);
  and and_27 (and_27_out, and_25_out, and_4_out);
  and and_28 (and_28_out, and_27_out, and_7_out);
  LED led_44 (.in(and_6_out));
  LED led_45 (.in(and_6_out));
  LED led_46 (.in(and_6_out));
  LED led_47 (.in(and_7_out));
  LED led_48 (.in(not_14_out));
  LED led_49 (.in(not_12_out));
  LED led_50 (.in(not_12_out));
  LED led_51 (.in(not_12_out));
  LED LOOPLINE_FEATHER_BULB_2 (.in(and_16_out));
  LED LOOPLINE_FEATHER_BULB_1 (.in(and_16_out));
  and and_29 (and_29_out, and_28_out, and_6_out);
  LED led_52 (.in(and_7_out));
  LED led_53 (.in(and_7_out));
  LED led_54 (.in(and_7_out));
  LED led_55 (.in(not_14_out));
  LED led_56 (.in(not_14_out));
  LED led_57 (.in(not_14_out));
  LED LOOPLINE_FEATHER_BULB_5 (.in(and_16_out));
  LED LOOPLINE_FEATHER_BULB_4 (.in(and_16_out));
  LED LOOPLINE_FEATHER_BULB_3 (.in(and_16_out));
  LED HOME_DANGER_ASPECT (.in(not_32_out));
  LED HOME_CAUTION_ASPECT (.in(and_30_out));
  and and_30 (and_30_out, or_7_out, not_33_out);
  not not_33 (not_33_out, and_31_out);
  and and_31 (and_31_out, not_5_out, and_29_out);
  LED HOME_PROCEED_ASPECT (.in(and_31_out));

  // Notes on the sheet:
  //   SINGLE CROSSOVER HOME SIGNAL FACING INPUT
  //   MAINLINE PLATFORM SECTION INPUT
  //   LOOPLINE PLATFORM SECTION INPUT
  //   MAINLINE STARTER SIGNAL TRAILING INPUTS
  //   MAINLINE ADVANCE STARTER INPUTS
  //   1ST BLOCK SECTION AFTER STATION SECTION
  //   SINGLE CROSSOVER PLATFORM STARTERS TRAILING INPUT 
  //   NON SIGNALLED AREAS
  //   SINGLE CROSSOVER LOOPLINE STARTER SIGNAL FACING INPUTS
  //   NOTE : THIS DESIGN IS VALID ONLY FOR ROUTES HAVING PSR AS 100 kmph.
  //   THIS IS A SHUNTING SWITCH LINE TO BE SET FOR MAIN TRACK MANUALLY IF IT IS 0 ELSE IT ACTS AS PROTECTEOR OF MAINLINE.
  //   PANEL DISPLAY
  //   MAINLINE STARTER OPERATIONAL OUTPUTS
  //   ADVANCE STARTER OPERATIONAL OUTPUTS
  //   LOOPLINE STARTER OPERATIONAL OUTPUTS
  //   HOME_SIGNAL ASPECT OUTPUTS
endmodule
