// Logisim project WARNER_DISTANT_SIGNALS.circ as structural Verilog: 1 circuit, main circuit main
module main (
  input  HOME_DISTANT_WARNER_DANGER,
  input  HOME_DISTANT_WARNER_CAUTION,
  input  HOME_DISTANT_WARNER_PROCEED,
  input  DANGER_WIRE_HEALTH
);

  wire and_1_out, and_2_out, and_3_out, and_4_out, and_5_out, not_1_out, not_2_out, not_3_out, not_4_out,
       not_5_out, or_1_out;

  and and_1 (and_1_out, HOME_DISTANT_WARNER_DANGER, DANGER_WIRE_HEALTH);
  LED DANGER_WIRE_HEALTH_OUTPUT (.in(DANGER_WIRE_HEALTH));
  not not_1 (not_1_out, and_1_out);
  and and_2 (and_2_out, HOME_DISTANT_WARNER_CAUTION, HOME_DISTANT_WARNER_PROCEED);
  not not_2 (not_2_out, and_2_out);
  and and_3 (and_3_out, HOME_DISTANT_WARNER_CAUTION, not_2_out, not_1_out);
  and and_4 (and_4_out, HOME_DISTANT_WARNER_PROCEED, not_2_out);
  not not_3 (not_3_out, and_3_out);
  not not_4 (not_4_out, and_1_out);
  and and_5 (and_5_out, not_3_out, and_4_out, not_4_out);
  not not_5 (not_5_out, and_4_out);
  LED DISTANT_WARNER_ATTENTION_Y2 (.in(and_3_out));
  LED DISTANT_WARNER_PROCEED_G1 (.in(and_5_out));
  or or_1 (or_1_out, and_3_out, not_5_out, and_1_out);
  LED DISTANT_WARNER_CAUTION_Y1 (.in(or_1_out));

  // Notes on the sheet:
  //   SENSOR INPUTS
  //   MAINTAINANCE OUTPUT
  //   DISTANT SIGNAL OPERATIONAL OUTPUTS
endmodule
